# Fritzing sketch Autonomous_Robot-01 (saved by Fritzing 0.9.3b)
breadboards: 1

parts:
  Part1 = Arduino Uno (Rev3)
  Part2 = Motor Driver 1A Dual TB6612FNG  # not connected
  hc-sr1 = hc-sr04  # not connected
  M1 = DC Motor  # not connected
  M2 = DC Motor  # not connected
  S1 = Toggle Switch [package=THT]
  LED1 = LED - 5mm [color="Green (570nm)" package="5 mm [THT]"]
  R1 = Resistor [tolerance=±5% resistance=330 package=THT]

nets:
  N1: Part1.GND, S1.COM, LED1.cathode
  N2: Part1.D2, R1.Pin_1
  N3: Part1.D4, S1.L1
  N4: LED1.anode, R1.Pin_0
